// Logisim project cpu.circ as structural Verilog: 2 circuits, main circuit main
module main (
  input  [31:0] INSTRUCTION,
  input  CLOCK,
  output [31:0] FETCH_ADDRESS,
  output [31:0] s0_Value,
  output [31:0] s1_Value,
  output [31:0] t0_Value,
  output [31:0] t1_Value,
  output [31:0] a0_Value,
  output [31:0] ra_Value,
  output [31:0] sp_Value
);

  wire Add, addASel, addBSel, Addi, addMemRW, addPCSel, And, Andi, ASel, Beq, Blt, Bltu, brEQ, brLT,
       comparator_1_eq, comparator_1_lt, comparator_2_eq, comparator_2_lt, Div, Jal, Jalr, Lb, Lh, Lui, Lw,
       MEM_p1, MEM_p2, MEM_p4, MEM_p10, MemRW, Mul, MulH, not_5_out, Or, Ori, PCSel, Rem, Sll, Slli, Slt,
       Slti, Srl, Srli, Sub, Sw, undriven, Xor, Xori;
  wire [1:0] addWBSel, WBSel;
  wire [2:0] ImmSel;
  wire [3:0] addALUSel, ALUSel, bit_extender_8_out;
  wire [24:0] demultiplexer_3_out1, Iimm, SBimm, Simm, Uimm, UJimm;
  wire [31:0] adder_1_out, bit_extender_3_out, bit_extender_4_out, bit_extender_5_out, bit_extender_6_out,
       demultiplexer_1_out0, demultiplexer_1_out1, demultiplexer_2_out0, demultiplexer_2_out1, immGen,
       main_2_result, MEM_p11, multiplexer_1_out, multiplexer_5_out, multiplexer_6_out, multiplexer_7_out,
       R1, R2;

  Multiplexer #(.width(32)) multiplexer_1 (
    .in0(adder_1_out), .in1(main_2_result), .out(multiplexer_1_out), .sel(PCSel));  // open: en
  Register #(.width(32)) PC (.D(multiplexer_1_out), .Q(FETCH_ADDRESS), .clk(CLOCK));  // open: en, clr
  not not_1 (addPCSel, Add);
  not not_2 (addASel, Add);
  not not_3 (addBSel, Add);
  assign addALUSel = {{3{1'b0}}, Add};  // Bit_Extender bit_extender_1
  not not_4 (addMemRW, Add);
  assign addWBSel = {{1{1'b0}}, Add};  // Bit_Extender bit_extender_2
  Adder #(.width(32)) adder_1 (.a(FETCH_ADDRESS), .b(32'h4), .out(adder_1_out));  // open: cin, cout
  assign bit_extender_3_out = {{20{1'b0}}, Iimm[24:13]};  // Bit_Extender bit_extender_3
  assign bit_extender_4_out = {{20{1'b0}}, {Simm[24:18], Simm[4:0]}};  // Bit_Extender bit_extender_4
  assign bit_extender_5_out = {{19{1'b0}}, {SBimm[24], SBimm[0], SBimm[23:18], SBimm[4:1], 1'b0}};  // Bit_Extender bit_extender_5
  assign bit_extender_6_out = {{11{1'b0}}, {UJimm[24], UJimm[12:5], UJimm[13], UJimm[23:14], 1'b0}};  // Bit_Extender bit_extender_6
  Demultiplexer #(.width(32)) demultiplexer_1 (
    .out0(demultiplexer_1_out0), .out1(demultiplexer_1_out1), .in(R1), .en(Bltu));  // open: sel
  Demultiplexer #(.width(32)) demultiplexer_2 (
    .out0(demultiplexer_2_out0), .out1(demultiplexer_2_out1), .in(R2), .en(Bltu));  // open: sel
  assign WBSel = {{1{1'b0}}, Addi};  // Bit_Extender bit_extender_7
  not not_5 (not_5_out, Addi);
  Demultiplexer #(.select(3), .width(25)) demultiplexer_3 (
    .out0(Iimm), .out1(demultiplexer_3_out1), .out2(SBimm), .out3(Uimm), .out4(UJimm),
    .in(INSTRUCTION[31:7]), .sel(ImmSel));  // open: out5, out6, out7, en
  Multiplexer #(.select(3), .width(32)) multiplexer_2 (
    .in0(bit_extender_3_out), .in1(bit_extender_4_out), .in2(bit_extender_5_out),
    .in3({Uimm[24:5], {12{1'b0}}}), .in4(bit_extender_6_out), .out(immGen), .sel(ImmSel));  // open: in5, in6, in7, en
  Comparator #(.width(32)) comparator_1 (
    .a(demultiplexer_1_out0), .b(demultiplexer_2_out0), .eq(comparator_1_eq), .lt(comparator_1_lt));  // open: gt
  Comparator #(.width(32), .mode("unsigned")) comparator_2 (
    .a(demultiplexer_1_out1), .b(demultiplexer_2_out1), .eq(comparator_2_eq), .lt(comparator_2_lt));  // open: gt
  not not_6 (PCSel, Addi);
  not not_7 (ASel, Addi);
  assign bit_extender_8_out = {{3{1'b0}}, Addi};  // Bit_Extender bit_extender_8
  not not_8 (MemRW, Addi);
  assign ImmSel = {{2{1'b0}}, not_5_out};  // Bit_Extender bit_extender_9
  Multiplexer multiplexer_3 (.in0(comparator_1_eq), .in1(comparator_2_eq), .out(brEQ), .sel(Bltu));  // open: en
  Multiplexer multiplexer_4 (.in0(comparator_1_lt), .in1(comparator_2_lt), .out(brLT), .sel(Bltu));  // open: en
  Shifter #(.width(4)) shifter_1 (.in(bit_extender_8_out), .\dist (2'b01), .out(ALUSel));
  regfile_main main_1 (
    .Read_Register_1__rs1(INSTRUCTION[19:15]), .Read_Register_2__rs2(INSTRUCTION[24:20]),
    .Write_Register__rd(INSTRUCTION[11:7]), .Write_Data(multiplexer_7_out), .Write_Enable(Addi),
    .Clock(CLOCK), .Read_Data_1(R1), .Read_Data_2(R2), .s1_Value(s1_Value), .t0_Value(t0_Value),
    .t1_Value(t1_Value), .a0_Value(a0_Value), .s0_Value(s0_Value), .ra_Value(ra_Value), .sp_Value(sp_Value));
  Multiplexer #(.width(32)) multiplexer_5 (.in0(R2), .in1(immGen), .out(multiplexer_5_out), .sel(Addi));  // open: en
  // NOT_Gate not_9 has open pins: in=undriven, out=open
  Multiplexer #(.width(32)) multiplexer_6 (
    .in0(R1), .in1(adder_1_out), .out(multiplexer_6_out), .sel(ASel));  // open: en
  control_unit Control_Unit (
    .Instruction(INSTRUCTION), .brEQ(brEQ), .brLT(brLT), .JALRtype(Jalr), .JALtype(Jal), .LUItype(Lui),
    .BLTUtype(Bltu), .BLTtype(Blt), .BEQtype(Beq), .SWtype(Sw), .ANDItype(Andi), .ORItype(Ori),
    .SRLItype(Srli), .XORItype(Xori), .SLTItype(Slti), .SLLItype(Slli), .ADDItype(Addi), .LWtype(Lw),
    .LHtype(Lh), .LBtype(Lb), .ANDtype(And), .REMtype(Rem), .ORtype(Or), .SRLtype(Srl), .DIVtype(Div),
    .XORtype(Xor), .SLTtype(Slt), .MULHtype(MulH), .SLLtype(Sll), .SUBtype(Sub), .MULtype(Mul), .ADDtype(Add));  // open: To_Instr_Mem, To_Instr_Mem_2
  // NOT_Gate not_10 has open pins: in=undriven, out=open
  alu_main main_2 (
    .Switch(ALUSel), .X(multiplexer_6_out), .Result(main_2_result), .Y(multiplexer_5_out));  // open: Equal
  // NOT_Gate not_11 has open pins: in=undriven, out=open
  // NOT_Gate not_12 has open pins: in=undriven, out=open
  // mem_main MEM: pin names not known; wires that end beside it: MEM_p1, MEM_p2, MEM_p2, MEM_p4, main_2_result, R2, MemRW, MEM_p4, CLOCK, MEM_p10, MEM_p11
  Multiplexer #(.select(2), .width(32)) multiplexer_7 (
    .in0(adder_1_out), .in1(main_2_result), .in2(MEM_p11), .out(multiplexer_7_out), .sel(WBSel));  // open: in3, en

  // Other names for the same wires on the sheet: a0[31:0] = a0_Value; addRegWEn = Add; clk = CLOCK;
  //   fetch_addr[31:0] = FETCH_ADDRESS; ra[31:0] = ra_Value; BSel = Addi; RegWEn = Addi; s0[31:0] = s0_Value;
  //   s1[31:0] = s1_Value; sp[31:0] = sp_Value; t0[31:0] = t0_Value; t1[31:0] = t1_Value

  // Notes on the sheet:
  //   Output
  //   These are outputs/inputs from run.circ
  //   Inputs
  //   These are DEBUG/TEST outputs from your circuit.
endmodule

module control_unit (
  input  [31:0] Instruction,
  input  brEQ,
  input  brLT,
  output JALRtype,
  output JALtype,
  output LUItype,
  output BLTUtype,
  output BLTtype,
  output BEQtype,
  output SWtype,
  output ANDItype,
  output ORItype,
  output SRLItype,
  output XORItype,
  output SLTItype,
  output SLLItype,
  output ADDItype,
  output LWtype,
  output LHtype,
  output LBtype,
  output ANDtype,
  output REMtype,
  output ORtype,
  output SRLtype,
  output DIVtype,
  output XORtype,
  output SLTtype,
  output MULHtype,
  output SLLtype,
  output SUBtype,
  output MULtype,
  output ADDtype,
  output To_Instr_Mem,
  output To_Instr_Mem_2
);

  wire demultiplexer_1_out0, demultiplexer_1_out1, demultiplexer_2_out0, demultiplexer_3_out0,
       demultiplexer_4_out0, demultiplexer_4_out1, demultiplexer_5_out1, demultiplexer_6_out0,
       demultiplexer_9_out1, demultiplexer_11_out0, demultiplexer_11_out1, demultiplexer_12_out0,
       demultiplexer_12_out1, demultiplexer_13_out0, demultiplexer_13_out1, demultiplexer_16_out0,
       demultiplexer_16_out1, demultiplexer_17_out0, demultiplexer_17_out1, demultiplexer_18_out0,
       demultiplexer_18_out1, demultiplexer_20_out0, demultiplexer_21_out0, demultiplexer_21_out1,
       demultiplexer_22_out0, demultiplexer_22_out1, demultiplexer_23_out0, demultiplexer_23_out1,
       demultiplexer_24_out0, demultiplexer_24_out1, demultiplexer_26_out0, Itype, LoadItype, Rtype;

  Demultiplexer demultiplexer_1 (
    .out0(demultiplexer_1_out0), .out1(demultiplexer_1_out1), .in(1'b1), .sel(Instruction[6]));  // open: en
  Demultiplexer demultiplexer_2 (
    .out0(demultiplexer_2_out0), .out1(JALtype), .in(demultiplexer_1_out1), .sel(Instruction[3]));  // open: en
  Demultiplexer demultiplexer_3 (
    .out0(demultiplexer_3_out0), .out1(Itype), .in(demultiplexer_4_out0), .sel(Instruction[4]));  // open: en
  Demultiplexer demultiplexer_4 (
    .out0(demultiplexer_4_out0), .out1(demultiplexer_4_out1), .in(demultiplexer_1_out0), .sel(Instruction[5]));  // open: en
  Demultiplexer demultiplexer_5 (
    .out0(SWtype), .out1(demultiplexer_5_out1), .in(demultiplexer_4_out1), .sel(Instruction[4]));  // open: en
  Demultiplexer demultiplexer_6 (
    .out0(demultiplexer_6_out0), .out1(JALRtype), .in(demultiplexer_2_out0), .sel(Instruction[2]));  // open: en
  Demultiplexer demultiplexer_7 (
    .out0(Rtype), .out1(LUItype), .in(demultiplexer_5_out1), .sel(Instruction[2]));  // open: en
  Demultiplexer demultiplexer_8 (.out1(LoadItype), .in(demultiplexer_3_out0), .sel(Instruction[1]));  // open: out0, en
  Demultiplexer demultiplexer_9 (
    .out0(BEQtype), .out1(demultiplexer_9_out1), .in(demultiplexer_6_out0), .sel(Instruction[14]));  // open: en
  Demultiplexer demultiplexer_10 (
    .out0(BLTtype), .out1(BLTUtype), .in(demultiplexer_9_out1), .sel(Instruction[13]));  // open: en
  Demultiplexer demultiplexer_11 (
    .out0(demultiplexer_11_out0), .out1(demultiplexer_11_out1), .in(demultiplexer_12_out0),
    .sel(Instruction[13]));  // open: en
  Demultiplexer demultiplexer_12 (
    .out0(demultiplexer_12_out0), .out1(demultiplexer_12_out1), .in(Itype), .sel(Instruction[14]));  // open: en
  Demultiplexer demultiplexer_13 (
    .out0(demultiplexer_13_out0), .out1(demultiplexer_13_out1), .in(demultiplexer_12_out1),
    .sel(Instruction[13]));  // open: en
  Demultiplexer demultiplexer_14 (
    .out0(ADDItype), .out1(SLLItype), .in(demultiplexer_11_out0), .sel(Instruction[12]));  // open: en
  Demultiplexer demultiplexer_15 (
    .out0(XORItype), .out1(SRLItype), .in(demultiplexer_13_out0), .sel(Instruction[12]));  // open: en
  Demultiplexer demultiplexer_16 (
    .out0(demultiplexer_16_out0), .out1(demultiplexer_16_out1), .in(demultiplexer_17_out0),
    .sel(Instruction[13]));  // open: en
  Demultiplexer demultiplexer_17 (
    .out0(demultiplexer_17_out0), .out1(demultiplexer_17_out1), .in(Rtype), .sel(Instruction[14]));  // open: en
  Demultiplexer demultiplexer_18 (
    .out0(demultiplexer_18_out0), .out1(demultiplexer_18_out1), .in(demultiplexer_17_out1),
    .sel(Instruction[13]));  // open: en
  Demultiplexer demultiplexer_19 (
    .out0(SLTItype), .in(demultiplexer_11_out1), .sel(Instruction[12]));  // open: out1, en
  Demultiplexer demultiplexer_20 (
    .out0(demultiplexer_20_out0), .out1(LWtype), .in(LoadItype), .sel(Instruction[13]));  // open: en
  Demultiplexer demultiplexer_21 (
    .out0(demultiplexer_21_out0), .out1(demultiplexer_21_out1), .in(demultiplexer_16_out0),
    .sel(Instruction[12]));  // open: en
  Demultiplexer demultiplexer_22 (
    .out0(demultiplexer_22_out0), .out1(demultiplexer_22_out1), .in(demultiplexer_16_out1),
    .sel(Instruction[12]));  // open: en
  Demultiplexer demultiplexer_23 (
    .out0(demultiplexer_23_out0), .out1(demultiplexer_23_out1), .in(demultiplexer_18_out0),
    .sel(Instruction[12]));  // open: en
  Demultiplexer demultiplexer_24 (
    .out0(demultiplexer_24_out0), .out1(demultiplexer_24_out1), .in(demultiplexer_18_out1),
    .sel(Instruction[12]));  // open: en
  Demultiplexer demultiplexer_25 (
    .out0(ORItype), .out1(ANDItype), .in(demultiplexer_13_out1), .sel(Instruction[12]));  // open: en
  Demultiplexer demultiplexer_26 (
    .out0(demultiplexer_26_out0), .out1(SUBtype), .in(demultiplexer_21_out0), .sel(Instruction[30]));  // open: en
  Demultiplexer demultiplexer_27 (
    .out0(SLLtype), .out1(MULHtype), .in(demultiplexer_21_out1), .sel(Instruction[25]));  // open: en
  Demultiplexer demultiplexer_28 (.out0(SLTtype), .in(demultiplexer_22_out0), .sel(Instruction[25]));  // open: out1, en
  Demultiplexer demultiplexer_29 (.in(demultiplexer_22_out1), .sel(Instruction[25]));  // open: out0, out1, en
  Demultiplexer demultiplexer_30 (
    .out0(XORtype), .out1(DIVtype), .in(demultiplexer_23_out0), .sel(Instruction[25]));  // open: en
  Demultiplexer demultiplexer_31 (.out0(SRLtype), .in(demultiplexer_23_out1), .sel(Instruction[25]));  // open: out1, en
  Demultiplexer demultiplexer_32 (
    .out0(ORtype), .out1(REMtype), .in(demultiplexer_24_out0), .sel(Instruction[25]));  // open: en
  Demultiplexer demultiplexer_33 (.out0(ANDtype), .in(demultiplexer_24_out1), .sel(Instruction[25]));  // open: out1, en
  Demultiplexer demultiplexer_34 (
    .out0(LBtype), .out1(LHtype), .in(demultiplexer_20_out0), .sel(Instruction[12]));  // open: en
  Demultiplexer demultiplexer_35 (
    .out0(ADDtype), .out1(MULtype), .in(demultiplexer_26_out0), .sel(Instruction[25]));  // open: en

  assign To_Instr_Mem = brEQ;
  assign To_Instr_Mem_2 = brLT;

  // Other names for the same wires on the sheet: Op1 = Instruction[1]; Op2 = Instruction[2]; Op3 = Instruction[3];
  //   Op4 = Instruction[4]; Op5 = Instruction[5]; Op6 = Instruction[6]; Func3_12 = Instruction[12];
  //   Func3_13 = Instruction[13]; Func3_14 = Instruction[14]; Func7_25 = Instruction[25]; Func7_30 = Instruction[30]

  // Notes on the sheet:
  //   ITypes
  //   UJTypes
  //   UTypes
  //   SBTypes
  //   STypes
  //   ITypes
  //   RTypes
endmodule
